// Digital circuit rom-test.dig as structural Verilog
module rom_test (
  input  [7:0] ADDR,
  input  in_3,
  input  in_6,
  input  in_7,
  input  in_8,
  input  in_9,
  output [31:0] IW,
  output out_4,
  output out_5,
  output [1:0] INUM,
  output ANY
);

  PriorityEncoder #(.Selector_Bits(2)) PriEnc (.in0(in_6), .in1(in_7), .in2(in_8), .in3(in_9), .num(INUM), .any(ANY));
  ROM #(.AddrBits(8), .Bits(32)) quadratic (.A(ADDR), .sel(1'b1), .D(IW));

  assign out_4 = in_3;
  assign out_5 = in_3;

  // Other names for the same wires on the sheet: done = in_3

  // Notes on the sheet:
  //   contents of quadratic (hex, n*v repeats v):
  //   2a502b3,2b282b3,2c50333,628533,d50533,8067,c0001073
endmodule
